# Fritzing sketch energy-monitor (saved by Fritzing 0.9.10b)
breadboards: 1

parts:
  ESP32 = Heltec WiFi LoRa 32 V2 [part_number=HTIT-WB32LA]
  R1 = Resistor [tolerance=±5% resistance=10k package="2010 [SMD]"]
  C1 = Electrolytic Capacitor [capacitance=10µF voltage=10V package="0605 [SMD, electrolytic]"]
  R2 = Resistor [tolerance=±5% resistance=10k package="2010 [SMD]"]
  R3 = Resistor [tolerance=±5% resistance=22 package="2010 [SMD]"]
  Audio_Jack = AUDIO-JACK2 [package=audio-jack]

nets:
  N1: ESP32.pin_15, R3.Pin_0, Audio_Jack.RING, Audio_Jack.TIP
  N2: ESP32.pin_16, ESP32.pin_17, R2.Pin_0
  N3: ESP32.GND, R1.Pin_0, C1.-
  N4: ESP32.pin_21, ESP32.pin_22
  N5: R1.Pin_1, C1.+, R2.Pin_1, R3.Pin_1, Audio_Jack.SLEEVE
